# Fritzing sketch project1 (saved by Fritzing 0.9.3b)
circuit board: 8.46667cm x 5.64444cm
breadboards: 1

parts:
  Part1 = Arduino Uno (Rev3)
  R1 = Resistor [tolerance=±5% resistance=220 package=THT]
  R2 = Resistor [tolerance=±5% resistance=220 package=THT]
  R3 = Resistor [tolerance=±5% resistance=220 package=THT]
  R4 = Resistor [tolerance=±5% resistance=220 package=THT]
  R5 = Resistor [tolerance=±5% resistance=220 package=THT]
  LED1 = LED - 5mm [color="Red (633nm)" package="5 mm [THT]"]
  LED2 = LED - 5mm [color="Red (633nm)" package="5 mm [THT]"]
  LED3 = LED - 5mm [color="Red (633nm)" package="5 mm [THT]"]
  LED4 = LED - 5mm [color="Red (633nm)" package="5 mm [THT]"]
  LED5 = LED - 5mm [color="Red (633nm)" package="5 mm [THT]"]
  S1 = Square Pushbutton
  S2 = Square Pushbutton
  R6 = Resistor [tolerance=±5% resistance=220 package=THT]
  R7 = Resistor [tolerance=±5% resistance=220 package=THT]
  HC-SR04_Sensor_1 = HC-SR04 Ultrasonic Distance Sensor

nets:
  N1: Part1.D8, S1.leg0, R6.Pin_1
  N2: Part1.D9_PWM, S2.leg0, R7.Pin_1
  N3: Part1.D12/MISO, HC-SR04_Sensor_1.ECHO
  N4: Part1.D13/SCK, HC-SR04_Sensor_1.TRIG
  GND: Part1.GND, R1.Pin_1, R2.Pin_1, R3.Pin_1, R4.Pin_1, R5.Pin_1, R6.Pin_0, R7.Pin_0, HC-SR04_Sensor_1.GND
  N5: Part1.D3_PWM, LED5.anode
  N6: Part1.D4, LED4.anode
  N7: Part1.D5_PWM, LED3.anode
  N8: Part1.D6_PWM, R2.Pin_0, LED2.cathode
  N9: Part1.D7, LED1.anode
  5V: Part1.5V, S1.leg1, S2.leg1, HC-SR04_Sensor_1.VCC
  N10: R1.Pin_0, LED1.cathode
  N11: R3.Pin_0, LED3.cathode
  N12: R4.Pin_0, LED4.cathode
  N13: R5.Pin_0, LED5.cathode
